// Logisim project archiMinimale.circ as structural Verilog: 1 circuit, main circuit main
module main (
  input  Mode_Manuel_Auto
);

  wire _0, adr0, adr4, and_1_out, beq, bgtz, blez, bne, branch, clock_1_out, comparator_3_eq,
       comparator_4_eq, emem, ereg, H, H_out, immrt, jr, keyboard_1_avail, multiplexer_8_out, not_1_out,
       not_2_out, not_3_out, or_1_out, rsshamt, rtrd, sns, tunnel, ualmem;
  wire [3:0] op;
  wire [4:0] multiplexer_2_out, num_rd, num_rs, num_rt, shamt;
  wire [5:0] co, nf;
  wire [6:0] keyboard_1_data;
  wire [31:0] adder_1_p1, adder_1_p2, adder_1_p3, adder_2_p2, bit_extender_1_out, bit_extender_2_out,
       bit_extender_3_out, imm32, mips_ram_1_p7, multiplexer_3_out, multiplexer_7_out, multiplexer_10_out,
       multiplexer_11_out, pc, res, rs, rt, w, wmem;

  Button u_H (.out(H_out));
  Clock clock_1 (.out(clock_1_out));
  Multiplexer #(.enable("false")) multiplexer_1 (.in0(H_out), .in1(clock_1_out), .out(H), .sel(Mode_Manuel_Auto));
  Button RaZ (.out(_0));
  not not_1 (not_1_out, ereg);
  Comparator #(.width(32)) comparator_1 (.a(res), .b(32'hffff0000), .eq(adr0));  // open: gt, lt
  // Probe on adr0
  // Probe on adr4
  // Probe on sns
  // Probe on rtrd
  // Probe on immrt
  // Probe on ualmem
  // Probe on branch
  // Probe on not_2_out
  not not_2 (not_2_out, ereg);
  // Probe on emem
  // Probe on op
  // Probe on shamt
  // Probe on rsshamt
  Multiplexer #(.width(5), .enable("false")) multiplexer_2 (
    .in0(num_rt), .in1(num_rd), .out(multiplexer_2_out), .sel(rtrd));
  and and_1 (and_1_out, adr0, keyboard_1_avail);
  // RegisterFile registerfile_1: pin names not known; wires that end beside it: w, H, not_1_out, multiplexer_2_out, num_rs, num_rt, _0, rs, rt, res[31:20]
  Keyboard keyboard_1 (.clk(H), .re(and_1_out), .clr(_0), .avail(keyboard_1_avail), .data(keyboard_1_data));
  Comparator #(.width(32)) comparator_2 (.a(res), .b(32'hffff0004), .eq(adr4));  // open: gt, lt
  Multiplexer #(.width(32), .enable("false")) multiplexer_3 (
    .in0(rt), .in1(wmem), .out(multiplexer_3_out), .sel(not_3_out));
  Comparator #(.width(32)) comparator_3 (.a(wmem), .b(32'h1), .eq(comparator_3_eq));  // open: gt, lt
  not not_3 (not_3_out, comparator_3_eq);
  Multiplexer #(.width(32), .enable("false")) multiplexer_4 (
    .in0(32'h1), .in1({{25{1'b0}}, keyboard_1_data}), .out(wmem), .sel(keyboard_1_avail));
  // MIPSProgramROM mipsprogramrom_1: pin names not known; wires that end beside it: pc, {co, num_rs, num_rt, num_rd, shamt, nf}
  // MIPS_RAM mips_ram_1: pin names not known; wires that end beside it: res[19:0], multiplexer_3_out, emem, 1'b1, H, _0, mips_ram_1_p7
  // Probe on {co, num_rs, num_rt, num_rd, shamt, nf}
  Comparator #(.width(32)) comparator_4 (.a(res), .b(32'hffff000c), .eq(comparator_4_eq));  // open: gt, lt
  Multiplexer #(.width(32), .enable("false")) multiplexer_5 (.in0(res), .in1(mips_ram_1_p7), .out(w), .sel(ualmem));
  TTY tty_1 (.data(wmem[6:0]), .clk(H), .we(comparator_4_eq), .clr(_0));
  assign bit_extender_1_out = {{16{num_rd[4]}}, {num_rd, shamt, nf}};  // Bit_Extender bit_extender_1
  Multiplexer #(.width(32), .enable("false")) multiplexer_6 (
    .in0(bit_extender_1_out), .in1(bit_extender_2_out), .out(imm32), .sel(sns));
  assign bit_extender_2_out = {{16{1'b0}}, {num_rd, shamt, nf}};  // Bit_Extender bit_extender_2
  and and_2 (beq, tunnel, branch);
  Multiplexer #(.width(32), .enable("false")) multiplexer_7 (
    .in0(adder_1_p1), .in1(adder_1_p3), .out(multiplexer_7_out), .sel(multiplexer_8_out));
  // Adder adder_1: pin names not known; wires that end beside it: adder_1_p1, adder_1_p2, adder_1_p3
  and and_3 (bne, ~tunnel, branch);  // AND_Gate
  // Adder adder_2: pin names not known; wires that end beside it: 32'h4, adder_2_p2, adder_1_p1
  Register #(.width(32), .trigger("falling")) register_1 (
    .D(multiplexer_7_out), .en(1'b1), .Q(adder_2_p2), .clk(H), .clr(_0));
  Shifter #(.width(32)) shifter_1 (.in(imm32), .\dist (5'b00010), .out(adder_1_p2));
  Multiplexer #(.select(2), .enable("false")) multiplexer_8 (
    .in0(beq), .in1(bne), .in2(blez), .in3(bgtz), .out(multiplexer_8_out), .sel(co[1:0]));
  and and_4 (blez, or_1_out, branch);
  or or_1 (or_1_out, tunnel, rs[31]);
  Multiplexer #(.width(32), .enable("false")) multiplexer_9 (.in0(adder_2_p2), .in1(rs), .out(pc), .sel(jr));
  and and_5 (bgtz, ~or_1_out, branch);  // AND_Gate
  assign bit_extender_3_out = {{27{1'b0}}, shamt};  // Bit_Extender bit_extender_3
  Multiplexer #(.width(32), .enable("false")) multiplexer_10 (
    .in0(imm32), .in1(rt), .out(multiplexer_10_out), .sel(immrt));
  // PLA pla_1: pin names not known; wires that end beside it: co, {rsshamt, emem, ereg, branch, ualmem, immrt, rtrd}
  Multiplexer #(.width(32), .enable("false")) multiplexer_11 (
    .in0(rs), .in1(bit_extender_3_out), .out(multiplexer_11_out), .sel(rsshamt));
  // Probe on res
  // Probe on pc
  // Probe on co
  // Probe on num_rs
  // Probe on rs
  // MIPS_ALU mips_alu_1: pin names not known; wires that end beside it: multiplexer_11_out, multiplexer_10_out, op, tunnel, res
  // Probe on num_rt
  // Probe on rt
  // Probe on shamt
  // Probe on nf
  // Probe on imm32
  // PLA PLA_2: pin names not known; wires that end beside it: {nf, co}, {jr, sns, op}
  // Probe on num_rd

  // Notes on the sheet:
  //   Ctrl + K pour activer l'horloge
  //   commandes
  //   mémoire de donnée
  //   Entrées/Sorties
  //   décomposition de l'opération MIPS
  //   on suppose que l'on a la valeur de rs UNIQUEMENT si on utilise rd --> ???
  //   détermination de la prochaine instruction (pc)
endmodule
