// Logisim project archiMinimale2.circ as structural Verilog: 1 circuit, main circuit main
module main (
  input  in_1,
  input  H,
  input  Raz
);

  wire registerfile_1_p7;
  wire [4:0] rd, rs, rt, shamt;
  wire [5:0] co, nf;
  wire [31:0] adder_1_p2, adder_1_p3, imm16, res;

  // Adder adder_1: pin names not known; wires that end beside it: 32'h4, adder_1_p2, adder_1_p3, adder_1_p2
  Register #(.width(32), .trigger("falling")) register_1 (
    .D(adder_1_p3), .en(1'b1), .Q(adder_1_p2), .clk(H), .clr(Raz));
  // Probe on adder_1_p2
  // RegisterFile registerfile_1: pin names not known; wires that end beside it: res, H, in_1, rt, rs, Raz, registerfile_1_p7
  // MIPSProgramROM mipsprogramrom_1: pin names not known; wires that end beside it: {co, rs, rt, rd, shamt, nf}
  // Probe on {co, rs, rt, rd, shamt, nf}
  // MIPS_ALU mips_alu_1: pin names not known; wires that end beside it: registerfile_1_p7, imm16, 4'b0011, res
  // Probe on imm16
  // Probe on rs
  assign imm16 = {{16{1'b0}}, {rd, shamt, nf}};  // Bit_Extender bit_extender_1
  // Probe on res
  // Probe on co
  // Probe on rs
  // Probe on rt
  // Probe on rd
  // Probe on shamt
  // Probe on nf
  // Probe on imm16

  // Other names for the same wires on the sheet: _0 = Raz
endmodule
